# Fritzing sketch schema (saved by Fritzing 1.0.6)

parts:
  R9 = Resistor [tolerance=±5% resistance=220 power=0.25W package=THT]
  R10 = Resistor [tolerance=±5% resistance=220 power=0.25W package=THT]
  R11 = Resistor [tolerance=±5% resistance=220 power=0.25W package=THT]
  R12 = Resistor [tolerance=±5% resistance=220 power=0.25W package=THT]
  R13 = Resistor [tolerance=±5% resistance=220 power=0.25W package=THT]
  R14 = Resistor [tolerance=±5% resistance=220 power=0.25W package=THT]
  R15 = Resistor [tolerance=±5% resistance=220 power=0.25W package=THT]
  R16 = Resistor [tolerance=±5% resistance=220 power=0.25W package=THT]
  U2 = 7-SEGMENT-4DIGIT [package=7-segment-4digit-5641]
  Raspberry_Pi2 = Raspberry Pi 2
  LCD2 = LCD screen
  LCM1602_IIC2 = LCM1602 IIC [part_number="LCM1602 IIC" chip_label="LCM1602 IIC" package="DIP (Dual Inline) [THT]"]
  S1 = Pushbutton [package="[THT]"]
  J1 = Piezo Speaker

nets:
  N1: R9.Pin_1, U2.B
  N2: R10.Pin_1, U2.F
  N3: R11.Pin_1, U2.A
  N4: R12.Pin_1, U2.G
  N5: R13.Pin_1, U2.C
  N6: R14.Pin_1, U2.D
  N7: R15.Pin_1, U2.DP
  N8: R16.Pin_1, U2.E
  N9: Raspberry_Pi2.GPIO2, LCM1602_IIC2.SDA
  N10: Raspberry_Pi2.GPIO3, LCM1602_IIC2.SCL
  N11: Raspberry_Pi2.GPIO4, J1.pin2
  GND: Raspberry_Pi2.GND, LCM1602_IIC2.GND, S1.Pin_3, S1.Pin_4, J1.pin1
  N12: Raspberry_Pi2.GPIO18, S1.Pin_1, S1.Pin_2
  5V: Raspberry_Pi2.5V, LCM1602_IIC2.VCC
  VSS: LCD2.VSS, LCM1602_IIC2.VSS
  VDD: LCD2.VDD, LCM1602_IIC2.VDD
  N13: LCD2.V0, LCM1602_IIC2.V0
  N14: LCD2.RS, LCM1602_IIC2.RS
  N15: LCD2.R/W, LCM1602_IIC2.RW
  N16: LCD2.E, LCM1602_IIC2.E
  N17: LCD2.DB0, LCM1602_IIC2.D0
  N18: LCD2.DB1, LCM1602_IIC2.D1
  N19: LCD2.DB2, LCM1602_IIC2.D2
  N20: LCD2.DB3, LCM1602_IIC2.D3
  N21: LCD2.DB4, LCM1602_IIC2.D4
  N22: LCD2.DB5, LCM1602_IIC2.D5
  N23: LCD2.DB6, LCM1602_IIC2.D6
  N24: LCD2.DB7, LCM1602_IIC2.D7
  N25: LCD2.LED+, LCM1602_IIC2.A
  N26: LCD2.LED-, LCM1602_IIC2.K
  N27: LCM1602_IIC2.LED_A, LCM1602_IIC2.LED_B

custom parts:
  7-SEGMENT-4DIGIT: if you need make parts, send me e-mail and write. Price 1 part=0.9 WMZ (http://www.wmtransfer.com/) ~ 0.9 Euro
  LCM1602 IIC: I2C-Module to use a 1602 or 2004 LCD on with the wire.h libory Serial LCD Modul
